# Fritzing sketch medidor de nivel NodeMCU-1 (saved by Fritzing 0.9.3b)
breadboards: 1

parts:
  Cheio = SWITCH-MOMENTARY-2 [package=reed_switch_pth]
  Vcc_5V = DC Power [voltage=5]
  Médio = SWITCH-MOMENTARY-2 [package=reed_switch_pth]
  LCM1602_IIC2 = LCM1602 IIC [part_number="LCM1602 IIC" chip_label="LCM1602 IIC" package="DIP (Dual Inline) [THT]"]
  R = Resistor [tolerance=±5% resistance=10k package="0805 [SMD]"]
  Vcc_3_3V = DC Power [voltage=5]
  U2 = NodeMCU V1.0
  R_2 = Resistor [tolerance=±5% resistance=10k package="0805 [SMD]"]
  J3 = Piezo Speaker
  R_3 = Resistor [tolerance=±5% resistance=10k package="0805 [SMD]"]
  LLC2 = Logic Level Converter [package="Breakout board"]
  LCD2 = LCD screen
  Vazio = SWITCH-MOMENTARY-2 [package=reed_switch_pth]

nets:
  N1: Cheio.1, Médio.1, Vcc_3_3V.V+, LLC2.LV, Vazio.1
  N2: Cheio.2, U2.D5, R_2.Pin_1
  N3: Vcc_5V.V+, U2.Vin
  GND: Vcc_5V.V-, LCM1602_IIC2.GND, R.Pin_0, Vcc_3_3V.V-, U2.GND, R_2.Pin_0, J3.pin1, R_3.Pin_0, LLC2.L-GND, LLC2.H-GND
  N4: Médio.2, R.Pin_1, U2.D6
  VSS: LCM1602_IIC2.VSS, LCD2.VSS
  VDD: LCM1602_IIC2.VDD, LCD2.VDD
  N5: LCM1602_IIC2.V0, LCD2.V0
  N6: LCM1602_IIC2.RS, LCD2.RS
  N7: LCM1602_IIC2.RW, LCD2.R/W
  N8: LCM1602_IIC2.E, LCD2.E
  N9: LCM1602_IIC2.D0, LCD2.DB0
  N10: LCM1602_IIC2.D1, LCD2.DB1
  N11: LCM1602_IIC2.D2, LCD2.DB2
  N12: LCM1602_IIC2.D3, LCD2.DB3
  N13: LCM1602_IIC2.D4, LCD2.DB4
  N14: LCM1602_IIC2.D5, LCD2.DB5
  N15: LCM1602_IIC2.D6, LCD2.DB6
  N16: LCM1602_IIC2.D7, LCD2.DB7
  N17: LCM1602_IIC2.A, LCD2.LED+
  N18: LCM1602_IIC2.K, LCD2.LED-
  N19: LCM1602_IIC2.VCC, LLC2.HV
  N20: LCM1602_IIC2.SDA, LLC2.HV4
  N21: LCM1602_IIC2.SCL, LLC2.HV3
  N22: U2.D1, LLC2.LV4
  N23: U2.D2, LLC2.LV3
  N24: U2.D4, J3.pin2
  N25: U2.D7, R_3.Pin_1, Vazio.2

custom parts:
  LCM1602 IIC: I2C-Module to use a 1602 or 2004 LCD on with the wire.h libory Serial LCD Modul
  NodeMCU V1.0: ESP8266 based NodeMCU
  Logic Level Converter: 5V to/from 3.3V logic level converter
